// Logisim project contador_mod_dez.circ as structural Verilog: 2 circuits, main circuit main
module main (
);

  wire and_1_out, clock_1_out, decode_1_out_5, decode_1_out_6, decode_1_out_7, decode_1_out_8,
       decode_1_out_9, decode_1_out_10, decode_1_out_11, j_k_ff_1_q, j_k_ff_1_qn, j_k_ff_2_q, j_k_ff_2_qn,
       j_k_ff_3_q, j_k_ff_3_qn, j_k_ff_4_q, j_k_ff_4_qn, not_1_out, not_2_out, not_3_out, not_4_out;

  and and_1 (and_1_out, j_k_ff_1_q, j_k_ff_3_q);
  J_K_Flip_Flop #(.trigger("falling")) j_k_ff_1 (
    .J(1'b1), .clk(j_k_ff_2_q), .K(1'b1), .Q(j_k_ff_1_q), .Qn(j_k_ff_1_qn), .reset(and_1_out));  // open: preset, en
  J_K_Flip_Flop #(.trigger("falling")) j_k_ff_2 (
    .J(1'b1), .clk(j_k_ff_3_q), .K(1'b1), .Q(j_k_ff_2_q), .Qn(j_k_ff_2_qn), .reset(and_1_out));  // open: preset, en
  J_K_Flip_Flop #(.trigger("falling")) j_k_ff_3 (
    .J(1'b1), .clk(j_k_ff_4_q), .K(1'b1), .Q(j_k_ff_3_q), .Qn(j_k_ff_3_qn), .reset(and_1_out));  // open: preset, en
  Clock clock_1 (.out(clock_1_out));
  J_K_Flip_Flop j_k_ff_4 (
    .J(1'b1), .clk(clock_1_out), .K(1'b1), .Q(j_k_ff_4_q), .Qn(j_k_ff_4_qn), .reset(and_1_out));  // open: preset, en
  not not_1 (not_1_out, j_k_ff_2_qn);
  not not_2 (not_2_out, j_k_ff_4_qn);
  not not_3 (not_3_out, j_k_ff_3_qn);
  not not_4 (not_4_out, j_k_ff_1_qn);
  decode decode_1 (
    .A(not_4_out), .in_2(not_1_out), .in_3(not_3_out), .in_4(not_2_out), .out_5(decode_1_out_5),
    .out_6(decode_1_out_6), .out_7(decode_1_out_7), .out_8(decode_1_out_8), .out_9(decode_1_out_9),
    .out_10(decode_1_out_10), .out_11(decode_1_out_11));
  _7_Segment_Display u_7_segment_display_1 (
    .g(decode_1_out_11), .f(decode_1_out_10), .a(decode_1_out_5), .b(decode_1_out_6), .e(decode_1_out_9),
    .d(decode_1_out_8), .c(decode_1_out_7), .dp(1'b0));
endmodule

// DECODE
module decode (
  input  A,
  input  in_2,
  input  in_3,
  input  in_4,
  output out_5,
  output out_6,
  output out_7,
  output out_8,
  output out_9,
  output out_10,
  output out_11
);

  wire and_1_out, and_2_out, and_3_out, and_4_out, and_5_out, and_6_out, and_7_out, and_8_out, and_9_out,
       and_10_out, and_11_out, and_12_out, and_13_out, and_14_out, and_15_out, and_16_out, and_17_out,
       and_18_out, and_19_out, and_20_out, and_21_out, and_22_out, and_23_out, and_24_out, and_25_out,
       and_26_out, not_1_out, not_2_out, not_3_out, not_4_out;

  not not_1 (not_1_out, A);
  not not_2 (not_2_out, in_3);
  not not_3 (not_3_out, in_2);
  not not_4 (not_4_out, in_4);
  and and_1 (and_1_out, not_3_out, not_2_out, not_4_out);
  and and_2 (and_2_out, A, not_3_out, not_2_out);
  and and_3 (and_3_out, not_1_out, in_2, in_4);
  and and_4 (and_4_out, not_1_out, in_3);
  and and_5 (and_5_out, not_3_out, not_2_out);
  and and_6 (and_6_out, not_1_out, not_2_out, not_4_out);
  and and_7 (and_7_out, not_1_out, in_3, in_4);
  and and_8 (and_8_out, not_1_out, not_3_out, in_3);
  and and_9 (and_9_out, not_3_out, not_2_out);
  and and_10 (and_10_out, not_1_out, not_2_out);
  and and_11 (and_11_out, not_1_out, in_3, in_4);
  and and_12 (and_12_out, not_1_out, in_2, in_3);
  and and_13 (and_13_out, not_3_out, not_2_out, not_4_out);
  and and_14 (and_14_out, not_1_out, not_3_out, in_3);
  and and_15 (and_15_out, not_1_out, in_3, not_4_out);
  and and_16 (and_16_out, not_1_out, in_2, not_2_out, in_4);
  and and_17 (and_17_out, not_3_out, not_4_out, not_2_out);
  and and_18 (and_18_out, not_1_out, in_3, not_4_out);
  and and_19 (and_19_out, not_1_out, not_2_out, not_4_out);
  and and_20 (and_20_out, not_1_out, in_2, not_4_out);
  and and_21 (and_21_out, A, not_3_out, not_2_out);
  and and_22 (and_22_out, not_1_out, in_2, not_2_out);
  and and_23 (and_23_out, not_1_out, in_2, not_2_out);
  and and_24 (and_24_out, A, not_3_out, not_2_out);
  and and_25 (and_25_out, not_1_out, not_3_out, in_3);
  and and_26 (and_26_out, not_1_out, in_3, not_4_out);
  or or_1 (out_5, and_1_out, and_2_out, and_3_out, and_4_out);
  or or_2 (out_9, and_17_out, and_18_out);
  or or_3 (out_10, and_19_out, and_20_out, and_21_out, and_22_out);
  or or_4 (out_11, and_23_out, and_24_out, and_25_out, and_26_out);
  or or_5 (out_6, and_5_out, and_6_out, and_7_out, and_8_out);
  or or_6 (out_7, and_9_out, and_10_out, and_11_out, and_12_out);
  or or_7 (out_8, and_13_out, and_14_out, and_15_out, and_16_out);
endmodule
