// Logisim project CIRC.circ as structural Verilog
module ULA (
  input  [2:0] \OPERAÇÃO ,
  input  [7:0] ENTRADA1,
  input  [7:0] ENTRADA2,
  output OVERFLOW,
  output [7:0] RESULTADO
);

  wire decodificador_1__0, decodificador_1__1, decodificador_1__2, decodificador_1__3, decodificador_1__4,
       decodificador_1__5, decodificador_1__6, decodificador_1__7;

  AND and_1 (.in_1(ENTRADA1), .in_2(ENTRADA2), .in_3(decodificador_1__0), .out_4(RESULTADO));
  OR or_1 (.in_1(ENTRADA1), .in_2(ENTRADA2), .out_4(RESULTADO), .in_3(decodificador_1__1));
  SOMA soma_1 (.in_1(ENTRADA1), .in_2(ENTRADA2), .out_4(RESULTADO), .ENABLE(decodificador_1__2), .OVERFLOW(OVERFLOW));
  \COMPARAÇÃO  \comparação_1  (.in_1(ENTRADA1), .in_2(ENTRADA2), .out_4(RESULTADO), .in_3(decodificador_1__3));
  COMPLEMTENTO_DE_DOIS complemtento_de_dois_1 (.in_1(ENTRADA1), .in_2(decodificador_1__4), .out_3(RESULTADO));
  \SUBTRAÇÃO  \subtração_1  (.A(ENTRADA1), .B(ENTRADA2), .ENABLE(decodificador_1__5), .out_4(RESULTADO));
  COPIA1 copia1_1 (.in_1(ENTRADA1), .in_2(ENTRADA2), .in_3(decodificador_1__6), .out_4(RESULTADO));
  COPIA2 copia2_1 (.in_1(ENTRADA1), .in_2(ENTRADA2), .in_3(decodificador_1__7), .out_4(RESULTADO));
  DECODIFICADOR decodificador_1 (
    .in_1(\OPERAÇÃO ), ._0(decodificador_1__0), ._1(decodificador_1__1), ._2(decodificador_1__2),
    ._3(decodificador_1__3), ._4(decodificador_1__4), ._5(decodificador_1__5), ._6(decodificador_1__6),
    ._7(decodificador_1__7));
endmodule

module DECODIFICADOR (
  input  [2:0] in_1,
  output _0,
  output _1,
  output _2,
  output _3,
  output _4,
  output _5,
  output _6,
  output _7
);

  wire nor_2_out, nor_3_out, nor_4_out, not_1_out, not_2_out, not_3_out;

  nor nor_1 (_0, in_1[0], in_1[1], in_1[2]);
  nor nor_2 (nor_2_out, in_1[2], in_1[1]);
  and and_1 (_1, nor_2_out, in_1[0]);
  nor nor_3 (nor_3_out, in_1[2], in_1[0]);
  and and_2 (_2, nor_3_out, in_1[1]);
  not not_1 (not_1_out, in_1[2]);
  and and_3 (_3, not_1_out, in_1[1], in_1[0]);
  and and_4 (_4, in_1[2], nor_4_out);
  nor nor_4 (nor_4_out, in_1[1], in_1[0]);
  and and_5 (_5, in_1[2], not_2_out, in_1[0]);
  not not_2 (not_2_out, in_1[1]);
  and and_6 (_6, in_1[2], in_1[1], not_3_out);
  not not_3 (not_3_out, in_1[0]);
  and and_7 (_7, in_1[2], in_1[1], in_1[0]);
endmodule

module AND (
  input  [7:0] in_1,
  input  [7:0] in_2,
  input  in_3,
  output [7:0] out_4
);

  wire [7:0] and_1_out;

  assign and_1_out = in_1 & in_2;  // AND_Gate and_1, 8 bits wide
  Transistor #(.\type ("n"), .gate("br"), .width(8)) transistor_1 (.in(and_1_out), .out(out_4), .gate(in_3));
endmodule

module OR (
  input  [7:0] in_1,
  input  [7:0] in_2,
  input  in_3,
  output [7:0] out_4
);

  wire [7:0] or_1_out;

  assign or_1_out = in_1 | in_2;  // OR_Gate or_1, 8 bits wide
  Transistor #(.\type ("n"), .gate("br"), .width(8)) transistor_1 (.in(or_1_out), .out(out_4), .gate(in_3));
endmodule

module SOMA (
  input  [7:0] in_1,
  input  [7:0] in_2,
  input  ENABLE,
  output [7:0] out_4,
  output OVERFLOW
);

  wire ms_1_carryout, sc_1_carryout, sc_2_carryout, sc_3_carryout, sc_4_carryout, sc_5_carryout,
       sc_6_carryout, sc_7_carryout;
  wire [7:0] ms_1_soma;

  Transistor #(.\type ("n")) transistor_1 (.in(sc_1_carryout), .out(OVERFLOW), .gate(ENABLE));
  SC sc_1 (.SOMA(ms_1_soma[7]), .CARRYOUT(sc_1_carryout), .A(in_1[7]), .B(in_2[7]), .CARRYIN(sc_2_carryout));
  SC sc_2 (.SOMA(ms_1_soma[6]), .CARRYOUT(sc_2_carryout), .A(in_1[6]), .B(in_2[6]), .CARRYIN(sc_3_carryout));
  SC sc_3 (.SOMA(ms_1_soma[5]), .CARRYOUT(sc_3_carryout), .A(in_1[5]), .B(in_2[5]), .CARRYIN(sc_4_carryout));
  SC sc_4 (.SOMA(ms_1_soma[4]), .CARRYOUT(sc_4_carryout), .A(in_1[4]), .B(in_2[4]), .CARRYIN(sc_5_carryout));
  SC sc_5 (.SOMA(ms_1_soma[3]), .CARRYOUT(sc_5_carryout), .A(in_1[3]), .B(in_2[3]), .CARRYIN(sc_6_carryout));
  SC sc_6 (.SOMA(ms_1_soma[2]), .CARRYOUT(sc_6_carryout), .A(in_1[2]), .B(in_2[2]), .CARRYIN(sc_7_carryout));
  SC sc_7 (.SOMA(ms_1_soma[1]), .CARRYOUT(sc_7_carryout), .A(in_1[1]), .B(in_2[1]), .CARRYIN(ms_1_carryout));
  MS ms_1 (.SOMA(ms_1_soma[0]), .CARRYOUT(ms_1_carryout), .A(in_1[0]), .B(in_2[0]));
  Transistor #(.\type ("n"), .width(8)) transistor_2 (.in(ms_1_soma), .out(out_4), .gate(ENABLE));
endmodule

// C. DE 2
module COMPLEMTENTO_DE_DOIS (
  input  [7:0] in_1,
  input  in_2,
  output [7:0] out_3
);

  wire [0:0] not_1_out;
  wire [7:0] not_2_out;

  not not_1 (not_1_out[0], 1'b0);
  assign not_2_out = ~in_1;  // NOT_Gate not_2, 8 bits wide
  SOMA soma_1 (.in_1(not_2_out), .in_2({{7{1'b0}}, not_1_out[0]}), .out_4(out_3), .ENABLE(in_2));  // open: OVERFLOW
endmodule

// COMP
module \COMPARAÇÃO  (
  input  [7:0] in_1,
  input  [7:0] in_2,
  input  in_3,
  output [7:0] out_4
);

  wire [7:0] and_1_out, and_2_out, not_1_out, not_2_out, or_1_out;

  assign not_1_out = ~in_1;  // NOT_Gate not_1, 8 bits wide
  assign not_2_out = ~in_2;  // NOT_Gate not_2, 8 bits wide
  assign and_1_out = not_1_out & in_2;  // AND_Gate and_1, 8 bits wide
  assign and_2_out = in_1 & not_2_out;  // AND_Gate and_2, 8 bits wide
  Transistor #(.\type ("n"), .gate("br"), .width(8)) transistor_1 (.in(or_1_out), .out(out_4), .gate(in_3));
  assign or_1_out = and_1_out | and_2_out;  // OR_Gate or_1, 8 bits wide
endmodule

module COPIA1 (
  input  [7:0] in_1,
  input  [7:0] in_2,
  input  in_3,
  output [7:0] out_4
);

  Transistor #(.\type ("n"), .gate("br"), .width(8)) transistor_1 (.in(in_1), .out(out_4), .gate(in_3));
endmodule

module COPIA2 (
  input  [7:0] in_1,
  input  [7:0] in_2,
  input  in_3,
  output [7:0] out_4
);

  Transistor #(.\type ("n"), .gate("br"), .width(8)) transistor_1 (.in(in_2), .out(out_4), .gate(in_3));
endmodule

// SUBTR.
module \SUBTRAÇÃO  (
  input  [7:0] A,
  input  [7:0] B,
  input  ENABLE,
  output [7:0] out_4
);

  wire msb_1_borrow_out, sbc_2_borrow_out, sbc_3_borrow_out, sbc_4_borrow_out, sbc_5_borrow_out,
       sbc_6_borrow_out, sbc_7_borrow_out;
  wire [7:0] msb_1_diferenca;

  SBC sbc_1 (.DIFERENCA(msb_1_diferenca[7]), .A(A[7]), .B(B[7]), .BORROW_IN(sbc_2_borrow_out));  // open: BORROW_OUT
  SBC sbc_2 (
    .DIFERENCA(msb_1_diferenca[6]), .BORROW_OUT(sbc_2_borrow_out), .A(A[6]), .B(B[6]),
    .BORROW_IN(sbc_3_borrow_out));
  SBC sbc_3 (
    .DIFERENCA(msb_1_diferenca[5]), .BORROW_OUT(sbc_3_borrow_out), .A(A[5]), .B(B[5]),
    .BORROW_IN(sbc_4_borrow_out));
  SBC sbc_4 (
    .DIFERENCA(msb_1_diferenca[4]), .BORROW_OUT(sbc_4_borrow_out), .A(A[4]), .B(B[4]),
    .BORROW_IN(sbc_5_borrow_out));
  SBC sbc_5 (
    .DIFERENCA(msb_1_diferenca[3]), .BORROW_OUT(sbc_5_borrow_out), .A(A[3]), .B(B[3]),
    .BORROW_IN(sbc_6_borrow_out));
  SBC sbc_6 (
    .DIFERENCA(msb_1_diferenca[2]), .BORROW_OUT(sbc_6_borrow_out), .A(A[2]), .B(B[2]),
    .BORROW_IN(sbc_7_borrow_out));
  SBC sbc_7 (
    .DIFERENCA(msb_1_diferenca[1]), .BORROW_OUT(sbc_7_borrow_out), .A(A[1]), .B(B[1]),
    .BORROW_IN(msb_1_borrow_out));
  MSB msb_1 (.DIFERENCA(msb_1_diferenca[0]), .BORROW_OUT(msb_1_borrow_out), .A(A[0]), .B(B[0]));
  Transistor #(.\type ("n"), .width(8)) transistor_1 (.in(msb_1_diferenca), .out(out_4), .gate(ENABLE));
endmodule

module SC (
  input  A,
  input  B,
  input  CARRYIN,
  output SOMA,
  output CARRYOUT
);

  wire and_1_out, and_2_out, and_3_out, xor_1_out;

  xor xor_1 (xor_1_out, A, B);
  and and_1 (and_1_out, A, CARRYIN);
  and and_2 (and_2_out, B, CARRYIN);
  and and_3 (and_3_out, A, B);
  xor xor_2 (SOMA, xor_1_out, CARRYIN);
  or or_1 (CARRYOUT, and_1_out, and_2_out, and_3_out);
endmodule

module MS (
  input  A,
  input  B,
  output SOMA,
  output CARRYOUT
);

  xor xor_1 (SOMA, A, B);
  and and_1 (CARRYOUT, A, B);
endmodule

module MSB (
  input  A,
  input  B,
  output DIFERENCA,
  output BORROW_OUT
);

  wire not_1_out;

  not not_1 (not_1_out, A);
  xor xor_1 (DIFERENCA, A, B);
  and and_1 (BORROW_OUT, not_1_out, B);
endmodule

module SBC (
  input  A,
  input  B,
  input  BORROW_IN,
  output DIFERENCA,
  output BORROW_OUT
);

  wire and_1_out, and_2_out, and_3_out, not_1_out, not_2_out, xor_1_out;

  not not_1 (not_1_out, A);
  not not_2 (not_2_out, A);
  xor xor_1 (xor_1_out, A, B);
  and and_1 (and_1_out, B, BORROW_IN);
  and and_2 (and_2_out, not_1_out, BORROW_IN);
  and and_3 (and_3_out, not_2_out, B);
  xor xor_2 (DIFERENCA, xor_1_out, BORROW_IN);
  or or_1 (BORROW_OUT, and_1_out, and_2_out, and_3_out);
endmodule
